# Fritzing sketch AdvPreAmp1 (saved by Fritzing 0.9.4)
circuit board: 6.23406cm x 6.02424cm
breadboards: 1

parts:
  18k = Resistor [tolerance=±5% resistance=15k package=THT]  # not connected
  8k2-1W = Resistor [tolerance=±5% resistance=6.8k package=THT]
  R4 = Resistor [tolerance=±5% resistance=22k package=THT]
  RedLED = LED - 3mm [color="Red (633nm)" package="3 mm [THT]"]
  47k = Resistor [tolerance=±5% resistance=47k package=THT]
  6k8 = Resistor [tolerance=±5% resistance=6.8k package=THT]
  12k = Resistor [tolerance=±5% resistance=15k package=THT]
  1k = Resistor [tolerance=±5% resistance=1k package=THT]
  560 = Resistor [tolerance=±5% resistance=470 package=THT]
  30pF = Ceramic Capacitor [capacitance=10pF voltage=35V part_number=30pF package="200 mil [THT, multilayer]"]
  330 = Resistor [tolerance=±5% resistance=330 package=THT]
  D1 = Rectifier Diode [part_number=1N4148 package="300 mil [THT]"]
  C2 = Ceramic Capacitor [capacitance=100nF package="200 mil [THT, multilayer]"]
  R12 = Resistor [tolerance=±5% resistance=1k package=THT]
  910 = Resistor [tolerance=±5% resistance=680 package=THT]  # not connected
  270k = Resistor [tolerance=±5% resistance=220k package=THT]
  270k_2 = Resistor [tolerance=±5% resistance=220 package=THT]
  15pF = Ceramic Capacitor [capacitance=10pF package="200 mil [THT, multilayer]"]
  680n = Ceramic Capacitor [capacitance=1µF package="200 mil [THT, multilayer]"]  # not connected
  R16 = Resistor [tolerance=±5% resistance=15k package=THT]
  R17 = Resistor [tolerance=±5% resistance=220 package=THT]
  270k_3 = Resistor [tolerance=±5% resistance=220k package=THT]
  910_2 = Resistor [tolerance=±5% resistance=680 package=THT]
  R20 = Resistor [tolerance=±5% resistance=1k package=THT]
  R21 = Resistor [tolerance=±5% resistance=220 package=THT]
  R22 = Resistor [tolerance=±5% resistance=220 package=THT]
  1k_2 = Resistor [tolerance=±5% resistance=1k package=THT]
  12k_2 = Resistor [tolerance=±5% resistance=15k package=THT]
  R25 = Resistor [tolerance=±5% resistance=220 package=THT]
  47k_2 = Resistor [tolerance=±5% resistance=47k package=THT]
  15k = Resistor [tolerance=±5% resistance=15k package=THT]  # not connected
  R28 = Resistor [tolerance=±5% resistance=220 package=THT]
  8k2-1W_2 = Resistor [tolerance=±5% resistance=220 package=THT]  # not connected
  18k_2 = Resistor [tolerance=±5% resistance=15k package=THT]  # not connected
  RedLED_2 = LED - 3mm [color="Red (633nm)" package="3 mm [THT]"]
  C8 = Ceramic Capacitor [capacitance=100nF package="200 mil [THT, multilayer]"]  # not connected
  C9 = Ceramic Capacitor [capacitance=100nF package="200 mil [THT, multilayer]"]
  C10 = Ceramic Capacitor [capacitance=100nF package="200 mil [THT, multilayer]"]
  C11 = Ceramic Capacitor [capacitance=10pF part_number=30pF package="200 mil [THT, multilayer]"]
  D2 = Rectifier Diode [part_number=1N4001 package="300 mil [THT]"]
  C12 = Ceramic Capacitor [capacitance=100nF package="200 mil [THT, multilayer]"]
  30pF_2 = Ceramic Capacitor [capacitance=10pF package="200 mil [THT, multilayer]"]  # not connected
  C14 = Tantalum Capacitor [capacitance=22µF voltage=16V package="200 mil [THT, tantalum]"]
  C15 = Tantalum Capacitor [capacitance=22µF voltage=16V package="200 mil [THT, tantalum]"]
  GreenLED1 = LED - 3mm [color="Red (633nm)" package="3 mm [THT]"]  # not connected
  GreenLED2 = LED - 3mm [color="Red (633nm)" package="3 mm [THT]"]  # not connected

nets:
  N1: 8k2-1W.Pin_0, RedLED.cathode
  N2: R4.Pin_0, 12k.Pin_0, 1k.Pin_0, R16.Pin_1, 1k_2.Pin_1, 12k_2.Pin_1, R28.Pin_0
  N3: RedLED.anode, 47k.Pin_1, 6k8.Pin_0, 560.Pin_0, 330.Pin_0
  N4: 30pF.1, D1.cathode
  N5: D1.anode, R12.Pin_1, C14.-
  N6: C2.1, 270k.Pin_0
  N7: 270k_2.Pin_0, 15pF.0
  N8: R17.Pin_0, C9.0
  N9: 270k_3.Pin_1, 910_2.Pin_1, C10.0
  N10: R20.Pin_0, D2.anode, C15.-
  N11: R21.Pin_1, C12.0
  N12: R22.Pin_1, R25.Pin_1, 47k_2.Pin_0, RedLED_2.anode
  N13: C11.0, D2.cathode
