# Fritzing sketch AdvPreAmp2 (saved by Fritzing 0.9.4)
circuit board: 6.23406cm x 6.02424cm
breadboards: 1

parts:
  18k = Resistor [tolerance=±5% resistance=15k package=THT]  # not connected
  8k2-1W = Resistor [tolerance=±5% resistance=6.8k package=THT]
  22k = Resistor [tolerance=±5% resistance=22k package=THT]
  RedLED = LED - 3mm [color="Red (633nm)" package="3 mm [THT]"]
  47k = Resistor [tolerance=±5% resistance=47k package=THT]
  6k8 = Resistor [tolerance=±5% resistance=6.8k package=THT]
  12k = Resistor [tolerance=±5% resistance=15k package=THT]
  10k = Resistor [tolerance=±5% resistance=10k package=THT]
  5k6 = Resistor [tolerance=±5% resistance=6.8k package=THT]
  30pF = Ceramic Capacitor [capacitance=10pF voltage=35V part_number=30pF package="200 mil [THT, multilayer]"]
  330 = Resistor [tolerance=±5% resistance=330 package=THT]
  47k_2 = Resistor [tolerance=±5% resistance=47k package=THT]
  820k = Resistor [tolerance=±5% resistance=680k package=THT]
  150pF = Ceramic Capacitor [capacitance=10pF package="200 mil [THT, multilayer]"]
  15k = Resistor [tolerance=±5% resistance=15k package=THT]
  820k_2 = Resistor [tolerance=±5% resistance=680k package=THT]  # not connected
  47k_3 = Resistor [tolerance=±5% resistance=47k package=THT]
  330_2 = Resistor [tolerance=±5% resistance=330 package=THT]
  5k6_2 = Resistor [tolerance=±5% resistance=6.8k package=THT]
  10k_2 = Resistor [tolerance=±5% resistance=10k package=THT]
  12k_2 = Resistor [tolerance=±5% resistance=15k package=THT]
  R25 = Resistor [tolerance=±5% resistance=220 package=THT]
  47k_4 = Resistor [tolerance=±5% resistance=47k package=THT]
  15k_2 = Resistor [tolerance=±5% resistance=15k package=THT]  # not connected
  22k_2 = Resistor [tolerance=±5% resistance=22k package=THT]
  8k2-1W_2 = Resistor [tolerance=±5% resistance=220 package=THT]  # not connected
  18k_2 = Resistor [tolerance=±5% resistance=15k package=THT]  # not connected
  RedLED_2 = LED - 3mm [color="Red (633nm)" package="3 mm [THT]"]
  C8 = Ceramic Capacitor [capacitance=100nF package="200 mil [THT, multilayer]"]  # not connected
  150pF_2 = Ceramic Capacitor [capacitance=10pF package="200 mil [THT, multilayer]"]  # not connected
  C11 = Ceramic Capacitor [capacitance=10pF part_number=30pF package="200 mil [THT, multilayer]"]
  C12 = Ceramic Capacitor [capacitance=100nF package="200 mil [THT, multilayer]"]
  GreenLED1 = LED - 3mm [color="Red (633nm)" package="3 mm [THT]"]  # not connected
  GreenLED2 = LED - 3mm [color="Red (633nm)" package="3 mm [THT]"]  # not connected

nets:
  N1: 8k2-1W.Pin_0, RedLED.cathode
  N2: 22k.Pin_0, 12k.Pin_0, 10k.Pin_0, 15k.Pin_1, 10k_2.Pin_1, 12k_2.Pin_1, 22k_2.Pin_0
  N3: RedLED.anode, 47k.Pin_1, 6k8.Pin_0, 5k6.Pin_0, 330.Pin_0
  N4: 30pF.1, 47k_2.Pin_0, 47k_3.Pin_0, C11.0
  N5: 820k.Pin_1, 150pF.1
  N6: 330_2.Pin_1, C12.0
  N7: 5k6_2.Pin_1, R25.Pin_1, 47k_4.Pin_0, RedLED_2.anode
