# Fritzing sketch AdvPreAmp3 (saved by Fritzing 0.9.4)
circuit board: 3.61389cm x 6.58509cm
breadboards: 1

parts:
  22k = Rotary Potentiometer (Large) [maximum_resistance=100kΩ package=THT]
  22k_2 = Rotary Potentiometer (Large) [maximum_resistance=100kΩ package=THT]
  100k = Rotary Potentiometer (Large) [maximum_resistance=100kΩ package=THT]
  22k_3 = Rotary Potentiometer (Large) [maximum_resistance=100kΩ package=THT]
  47nF = Ceramic Capacitor [capacitance=10nF package="200 mil [THT, multilayer]"]
  47nF_2 = Ceramic Capacitor [capacitance=10nF package="200 mil [THT, multilayer]"]
  47nF_3 = Ceramic Capacitor [capacitance=10nF package="200 mil [THT, multilayer]"]
  47nF_4 = Ceramic Capacitor [capacitance=10nF package="200 mil [THT, multilayer]"]
  12k = Resistor [tolerance=±5% resistance=15k package=THT]
  12k_2 = Resistor [tolerance=±5% resistance=15k package=THT]
  12k_3 = Resistor [tolerance=±5% resistance=15k package=THT]
  12k_4 = Resistor [tolerance=±5% resistance=15k package=THT]
  3n3F = Ceramic Capacitor [capacitance=1nF package="200 mil [THT, multilayer]"]
  3n3F_2 = Ceramic Capacitor [capacitance=1nF package="200 mil [THT, multilayer]"]
  3n3F_3 = Ceramic Capacitor [capacitance=1nF package="200 mil [THT, multilayer]"]
  3n3F_4 = Ceramic Capacitor [capacitance=1nF package="200 mil [THT, multilayer]"]
  2k7 = Resistor [tolerance=±5% resistance=2.2k package=THT]
  2k7_2 = Resistor [tolerance=±5% resistance=2.2k package=THT]
  2k7_3 = Resistor [tolerance=±5% resistance=2.2k package=THT]
  2k7_4 = Resistor [tolerance=±5% resistance=2.2k package=THT]
  100k_2 = Rotary Potentiometer (Large) [maximum_resistance=100kΩ package=THT]
  100nF = Ceramic Capacitor [capacitance=100nF package="200 mil [THT, multilayer]"]  # not connected
  100nF_2 = Ceramic Capacitor [capacitance=100nF package="200 mil [THT, multilayer]"]
  3uF = Ceramic Capacitor [capacitance=2.2µF package="200 mil [THT, multilayer]"]
  3uF_2 = Ceramic Capacitor [capacitance=2.2µF package="200 mil [THT, multilayer]"]
  220 = Resistor [tolerance=±5% resistance=220 package=THT]
  220_2 = Resistor [tolerance=±5% resistance=220 package=THT]
  1uF = Ceramic Capacitor [capacitance=1µF package="200 mil [THT, multilayer]"]  # not connected
  1uF_2 = Ceramic Capacitor [capacitance=1µF package="200 mil [THT, multilayer]"]  # not connected
  22k_4 = Rotary Potentiometer (Large) [maximum_resistance=100kΩ package=THT]

nets:
  N1: 22k.leg2, 22k_4.leg2
  N2: 22k_2.leg1, 3n3F_2.1
  N3: 22k_2.wiper, 100nF_2.1
  N4: 22k_2.leg2, 3n3F_4.1
  N5: 100k.leg1, 47nF_2.0, 12k_3.Pin_1
  N6: 100k.wiper, 47nF_2.1, 47nF_3.1
  N7: 100k.leg2, 47nF_3.0, 12k_4.Pin_1
  N8: 22k_3.leg2, 3n3F_3.1
  N9: 47nF.0, 12k.Pin_1, 100k_2.leg2
  N10: 47nF.1, 47nF_4.1
  N11: 47nF_4.0, 12k_2.Pin_1, 100k_2.leg1
  N12: 12k.Pin_0, 220.Pin_0
  N13: 12k_2.Pin_0, 2k7.Pin_0
  N14: 12k_4.Pin_0, 2k7_2.Pin_0
  N15: 3n3F.0, 2k7_4.Pin_1
  N16: 3n3F_2.0, 2k7.Pin_1
  N17: 3n3F_3.0, 2k7_2.Pin_1
  N18: 3n3F_4.0, 2k7_3.Pin_1
  N19: 3uF.0, 220.Pin_1
  N20: 3uF_2.0, 220_2.Pin_1
